# Fritzing sketch BabyPod (saved by Fritzing 1.0.3b)

parts:
  Piezo1 = Piezo Speaker - PC Mount [part_number=COM-07950]
  Part1 = Adafruit SPI Flash SD Card [part_number="Adafruit #4899"]
  Part2 = Adafruit ESP32-S3 Feather [part_number="Adafruit #5323"]
  Part3 = Adafruit PCF8523 STEMMA QT [part_number="Adafruit #5189"]
  Adafruit_ANO_Rotary_Encoder_to_I2C_Adapter_-_No_Encoder1 = Adafruit ANO Rotary Encoder to I2C Adapter - No Encoder [part_number=#5740]
  LCD2004-I2C1 = LCD2004-I2C
  Part4 = Lithium Ion Polymer Battery 3.7v 2500mAh [part_number=328]

nets:
  GND: Piezo1.GND, Part1.GND, Part2.GND, Part3.GND, Adafruit_ANO_Rotary_Encoder_to_I2C_Adapter_-_No_Encoder1.GND, LCD2004-I2C1.GND, Part4.negative
  N1: Piezo1.VCC, Part2.A3
  VIN: Part1.VIN, Part2.3.3V
  N2: Part1.SCK, Part2.SCK
  N3: Part1.MISO_3.3V, Part2.MISO
  N4: Part1.MOSI, Part2.MOSI
  N5: Part1.SS, Part2.D10
  VCC: Part2.VSENSOR, Part3.VCC, Adafruit_ANO_Rotary_Encoder_to_I2C_Adapter_-_No_Encoder1.VCC, LCD2004-I2C1.VCC
  N6: Part2.SDA, Part3.SDA, Adafruit_ANO_Rotary_Encoder_to_I2C_Adapter_-_No_Encoder1.SDA, LCD2004-I2C1.SDA
  N7: Part2.SCL, Part3.SCL, Adafruit_ANO_Rotary_Encoder_to_I2C_Adapter_-_No_Encoder1.SCL, LCD2004-I2C1.SCL
  N8: Part2.D11, Adafruit_ANO_Rotary_Encoder_to_I2C_Adapter_-_No_Encoder1.INT
  N9: Part2.VBAT, Part4.positive

custom parts:
  Piezo Speaker - PC Mount: This is a small 12mm round speaker that operates around the audible 2kHz range. You can use these speakers to create simple music or user interfaces. Each speaker is PTH solderable and requires an operating voltage of 3.5-5V with a mean current of 35mA max. These speakers also have a typical sound output of 95 dBA and a coil resistance of 42 ±6.3 ohms.
  Adafruit SPI Flash SD Card: This breakout is for a fascinating chip - it looks like an SPI Flash storage chip (like the GD25Q16) but its really an SD card, in an SMT chip format. What that means is that you wire up like an SD card breakout, and use the SD card libraries you already have for your microcontroller. For example, you can use the built in SD library in Arduino, or for CircuitPython we have an sdcard library.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
  Adafruit ESP32-S3 Feather: The ESP32-S3 has arrived in Feather format - and what a great way to get started with this powerful new chip from Espressif! With dual 240 MHz cores, WiFi and BLE support, and native USB, this Feather is great for powering your IoT projects. That's right - it's the new Adafruit ESP32-S3 Feather! With native USB and 8 MB flash, this board will let you upgrade your existing ESP32 projects.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
  Adafruit PCF8523 STEMMA QT: This is a great battery-backed real time clock (RTC) that allows your microcontroller project to keep track of time even if it is reprogrammed, or if the power is lost. Perfect for data-logging, clock-building, time stamping, timers, and alarms, etc. Equipped with PCF8523 RTC - it can run from 3.3V or 5V power & logic! We've had a breakout board version of this RTC for a while, but we want to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
  Adafruit ANO Rotary Encoder to I2C Adapter - No Encoder: The ANO rotary encoder wheel is a funky user interface element, reminiscent of the original clicking scroll wheel interface on the first iPods. It's a nifty kit, but the pin-out is a little odd - and there's a ton of pins needed to connect to the rotary encoder and 5 button switches. This Stemma QT breakout makes all that frustration go away - solder in the ANO Directional Navigation and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
  LCD2004-I2C: A standard character display with 4x20 characters. Comes in many colors with LCM2004 IIC attached.
  Lithium Ion Polymer Battery 3.7v 2500mAh: Lithium ion polymer (also known as 'lipo' or 'lipoly') batteries are thin, light and powerful. The output ranges from 4.2V when completely charged to 3.7V. This battery has a capacity of 2500mAh for a total of about 10 Wh. The batteries come pre-attached with a genuine 2-pin JST-PH connector as shown and include the necessary protection circuitry.
